# Fritzing sketch BusDirectorLoRaBv7 (saved by Fritzing 0.9.9b)
breadboards: 1

parts:
  Argon1 = Particle Argon
  Part1 = Adafruit PA1010D Mini GPS Module [part_number="Adafruit #4415"]
  LoRa = ossoyoo-lora-module

nets (from the schematic view):
  VCC: Argon1.3.3V, Part1.VCC, LoRa.VCC
  GND: Argon1.GND, Part1.GND, LoRa.GND
  N1: Argon1.RX, LoRa.RXD
  N2: Argon1.TX, LoRa.TXD
  N3: Argon1.SDA, Part1.SDA
  N4: Argon1.SCL, Part1.SCL

custom parts:
  Particle Argon: The Argon is a powerful Wi-Fi enabled development board that can act as either a standalone Wi-Fi endpoint or Wi-Fi enabled gateway for Particle Mesh networks. It is based on the Nordic nRF52840 and has built-in battery charging circuitry so it’s easy to connect a Li-Po and deploy your local network in minutes. The Argon is great for connecting existing projects to the Particle Device Cloud or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
  Adafruit PA1010D Mini GPS Module: This miniature GPS breakout is only 1" x 1" (~ 25mm x 25mm) but houses a complete GPS/GNSS solution with both I2C and UART interfaces. There's even an antenna on top so it's plug and play! Support for GPS, GLONASS, GALILEO, QZSS -165 dBm sensitivity, up to 10 Hz updates Up to 210 PRN channels with 99 search channels and 33 simultaneous tracking channels 5V friendly design and only 30mA current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
  ossoyoo-lora-module: Osoyoo Long Distance wireless transceiver Uart LoRa Module.
