# Fritzing sketch BusDirectorLoRaHV5 (saved by Fritzing 0.9.9b)
breadboards: 1

parts:
  Argon1 = Particle Argon
  U1 = ENCODER_RGB [package=encoder_led_2]
  OLED_I2C1 = OLED 128x64 I2C Monochrome Display

nets:
  GND: Argon1.GND, U1.C, OLED_I2C1.GND
  N1: Argon1.MO, U1.A
  N2: Argon1.MI, U1.B#2
  N3: Argon1.VUSB, OLED_I2C1.VDD

custom parts:
  Particle Argon: The Argon is a powerful Wi-Fi enabled development board that can act as either a standalone Wi-Fi endpoint or Wi-Fi enabled gateway for Particle Mesh networks. It is based on the Nordic nRF52840 and has built-in battery charging circuitry so it’s easy to connect a Li-Po and deploy your local network in minutes. The Argon is great for connecting existing projects to the Particle Device Cloud or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
  ENCODER_RGB: SparkFun RGB rotary Encoder
