# Fritzing sketch BusDirectorLoRaHv8 (saved by Fritzing 0.9.9b)
breadboards: 1

parts:
  Argon1 = Particle Argon
  Encoder = ENCODER_RGB [package=encoder_led_2]
  LoRa = ossoyoo-lora-module
  OLED_I2C1 = OLED 128x64 I2C Monochrome Display
  M1 = Vibration Motor- ROB-08449 [package=vibe-motor-mobile]  # not connected

nets (from the schematic view):
  3.3V: Argon1.3.3V, LoRa.VCC
  GND: Argon1.GND, Encoder.C, LoRa.GND
  N1: Argon1.MI, Encoder.A
  N2: Argon1.RX, LoRa.RXD
  N3: Argon1.TX, LoRa.TXD
  N4: Argon1.SDA, OLED_I2C1.SDA
  N5: Argon1.SCL, OLED_I2C1.SCK
  N6: Argon1.VUSB, OLED_I2C1.VDD

custom parts:
  Particle Argon: The Argon is a powerful Wi-Fi enabled development board that can act as either a standalone Wi-Fi endpoint or Wi-Fi enabled gateway for Particle Mesh networks. It is based on the Nordic nRF52840 and has built-in battery charging circuitry so it’s easy to connect a Li-Po and deploy your local network in minutes. The Argon is great for connecting existing projects to the Particle Device Cloud or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
  ENCODER_RGB: SparkFun RGB rotary Encoder
  ossoyoo-lora-module: Osoyoo Long Distance wireless transceiver Uart LoRa Module.
  Vibration Motor- ROB-08449: Vibration Motor- Mobile vibration motor with Rubber cover. Motor pin in for copper pad connectors, but can be use as THT.
