# Fritzing sketch MACBluSeekerv1 (saved by Fritzing 0.9.9b)
breadboards: 1

parts:
  M2 = BMP280
  Argon1 = Particle Argon

nets (from the breadboard view):
  GND: M2.VIN, M2.GND, Argon1.GND
  N1: M2.SCL, Argon1.SDA
  N2: M2.SDA, Argon1.SCL

custom parts:
  BMP280: Temperature Humidity Barometric presure Sensor, I2C
  Particle Argon: The Argon is a powerful Wi-Fi enabled development board that can act as either a standalone Wi-Fi endpoint or Wi-Fi enabled gateway for Particle Mesh networks. It is based on the Nordic nRF52840 and has built-in battery charging circuitry so it’s easy to connect a Li-Po and deploy your local network in minutes. The Argon is great for connecting existing projects to the Particle Device Cloud or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
